# Fritzing sketch AirBox (saved by Fritzing 0.9.3b)
breadboards: 1

parts:
  U1 = RF_RX
  U2 = RF-LINK_TX [package=rf-link_tx]
  Bauteil1 = ESP32 Module Testbed
  SD1 = SD Card [part_number=sdcard]

nets:
  GND: U1.connector1, U2.GND, Bauteil1.GND#51, SD1.GND, SD1.GND1
  N1: U1.connector2, Bauteil1.IO0
  N2: U1.connector4, U2.+5V
  3V3: Bauteil1.3V3, SD1.VCC
  N3: Bauteil1.SVN, Bauteil1.IO16
  N4: Bauteil1.IO34, Bauteil1.IO17
  N5: Bauteil1.IO5, SD1.CS
  N6: Bauteil1.IO18, SD1.SCK
  N7: Bauteil1.IO19, SD1.DO
  N8: Bauteil1.IO23, SD1.DI

custom parts:
  RF-LINK_TX: Common RF transmitter of the 315.00Mhz varity
  ESP32 Module Testbed: The ESP32 Module Testbed is a breadboard compatible breakout board for the ESP-WROOM-03 ESP32 module. The ESP32 is a WiFi and Bluetooth-enabled 32-bit, dual-core microcontroller.
